// Digital circuit 1b_ADDER.dig as structural Verilog
module _1b_ADDER (
  input  A,
  input  B,
  input  Cin,
  output O,
  output C
);

  wire and_1_out, and_2_out, xor_1_out;

  xor xor_1 (xor_1_out, A, B);
  and and_1 (and_1_out, A, B);
  and and_2 (and_2_out, xor_1_out, Cin);
  xor xor_2 (O, xor_1_out, Cin);
  or or_1 (C, and_1_out, and_2_out);
endmodule
