// Digital circuit ADDER.dig as structural Verilog
module ADDER (
  input  [7:0] A,
  input  [7:0] B,
  input  Cin,
  output [7:0] O
);

  wire _1b_adder_1_c, _1b_adder_2_c, _1b_adder_3_c, _1b_adder_4_c, _1b_adder_5_c, _1b_adder_6_c,
       _1b_adder_7_c;

  _1b_ADDER _1b_adder_1 (.A(A[0]), .B(B[0]), .Cin(Cin), .O(O[0]), .C(_1b_adder_1_c));
  _1b_ADDER _1b_adder_2 (.A(A[1]), .B(B[1]), .Cin(_1b_adder_1_c), .O(O[1]), .C(_1b_adder_2_c));
  _1b_ADDER _1b_adder_3 (.A(A[2]), .B(B[2]), .Cin(_1b_adder_2_c), .O(O[2]), .C(_1b_adder_3_c));
  _1b_ADDER _1b_adder_4 (.A(A[3]), .B(B[3]), .Cin(_1b_adder_3_c), .O(O[3]), .C(_1b_adder_4_c));
  _1b_ADDER _1b_adder_5 (.A(A[4]), .B(B[4]), .Cin(_1b_adder_4_c), .O(O[4]), .C(_1b_adder_5_c));
  _1b_ADDER _1b_adder_6 (.A(A[5]), .B(B[5]), .Cin(_1b_adder_5_c), .O(O[5]), .C(_1b_adder_6_c));
  _1b_ADDER _1b_adder_7 (.A(A[6]), .B(B[6]), .Cin(_1b_adder_6_c), .O(O[6]), .C(_1b_adder_7_c));
  _1b_ADDER _1b_adder_8 (.A(A[7]), .B(B[7]), .Cin(_1b_adder_7_c), .O(O[7]));  // open: C
endmodule
