// Digital circuit ALU.dig as structural Verilog
module ALU (
  input  [7:0] A,
  input  [7:0] B,
  input  SUB,
  output [7:0] O,
  output NEG,
  output ZERO
);

  wire and_1_out, not_1_out, not_2_out, not_3_out, not_4_out, not_5_out, not_6_out, not_7_out, not_8_out;
  wire [7:0] xor_1_out;

  xor xor_1 (xor_1_out[0], B[0], SUB);
  xor xor_2 (xor_1_out[1], B[1], SUB);
  xor xor_3 (xor_1_out[2], B[2], SUB);
  xor xor_4 (xor_1_out[3], B[3], SUB);
  xor xor_5 (xor_1_out[4], B[4], SUB);
  xor xor_6 (xor_1_out[5], B[5], SUB);
  xor xor_7 (xor_1_out[6], B[6], SUB);
  xor xor_8 (xor_1_out[7], B[7], SUB);
  ADDER adder_1 (.A(A), .B(xor_1_out), .Cin(xor_1_out[7]), .O({O[7:1], NEG}));
  not not_1 (not_1_out, NEG);
  not not_2 (not_2_out, O[1]);
  not not_3 (not_3_out, O[2]);
  not not_4 (not_4_out, O[3]);
  not not_5 (not_5_out, O[4]);
  not not_6 (not_6_out, O[5]);
  not not_7 (not_7_out, O[6]);
  not not_8 (not_8_out, O[7]);
  and and_1 (and_1_out, not_1_out, not_2_out, not_3_out, not_4_out, not_5_out);
  and and_2 (ZERO, and_1_out, not_6_out, not_7_out, not_8_out);

  assign O[0] = NEG;
endmodule
