// Digital circuit DFlipFlop.dig as structural Verilog
module DFlipFlop (
  input  D,
  input  CLK,
  output OUT
);

  wire dlatch_1_out, not_1_out;

  DLatch dlatch_1 (.D(D), .ENB(CLK), .OUT(dlatch_1_out));
  not not_1 (not_1_out, CLK);
  DLatch dlatch_2 (.D(dlatch_1_out), .ENB(not_1_out), .OUT(OUT));
endmodule
