// Digital circuit DLatch.dig as structural Verilog
module DLatch (
  input  D,
  input  ENB,
  output OUT
);

  wire and_1_out, and_2_out, not_1_out;

  not not_1 (not_1_out, D);
  and and_1 (and_1_out, D, ENB);
  and and_2 (and_2_out, not_1_out, ENB);
  SRLatch srlatch_1 (.S(and_1_out), .R(and_2_out), .Q(OUT));
endmodule
