// Digital circuit SRLatch.dig as structural Verilog
module SRLatch (
  input  S,
  input  R,
  output Q
);

  wire nor_2_out;

  nor nor_1 (Q, R, nor_2_out);
  nor nor_2 (nor_2_out, Q, S);
endmodule
